// Logisim project 4bitcpu.circ as structural Verilog: 4 circuits, main circuit fourbitadder
module fourbitadder (
  input  Carry_In,
  input  B4,
  input  B3,
  input  B2,
  input  B1,
  input  A4,
  input  A3,
  input  A2,
  input  A1,
  input  Clock,
  output Overflow,
  output O1,
  output O2,
  output O3,
  output O4
);

  wire and_1_out, and_2_out, and_3_out, and_4_out, and_5_out, and_6_out, and_7_out, and_8_out, and_9_out,
       and_10_out, and_11_out, and_12_out, and_13_out, and_14_out, and_15_out, and_16_out, or_2_out,
       or_3_out, or_4_out, xor_1_out, xor_2_out, xor_3_out, xor_4_out;

  and and_1 (and_1_out, B4, Clock);
  and and_2 (and_2_out, A4, Clock);
  and and_3 (and_3_out, B1, Clock);
  and and_4 (and_4_out, A1, Clock);
  and and_5 (and_5_out, Clock, B3);
  and and_6 (and_6_out, Clock, A3);
  and and_7 (and_7_out, Clock, B2);
  and and_8 (and_8_out, A2, Clock);
  and and_9 (and_9_out, and_1_out, and_2_out);
  xor xor_1 (xor_1_out, and_2_out, and_1_out);
  and and_10 (and_10_out, and_5_out, and_6_out);
  xor xor_2 (xor_2_out, and_6_out, and_5_out);
  and and_11 (and_11_out, and_7_out, and_8_out);
  xor xor_3 (xor_3_out, and_8_out, and_7_out);
  and and_12 (and_12_out, and_3_out, and_4_out);
  xor xor_4 (xor_4_out, and_4_out, and_3_out);
  and and_13 (and_13_out, or_2_out, xor_1_out);
  xor xor_5 (O4, xor_1_out, or_2_out);
  and and_14 (and_14_out, or_3_out, xor_2_out);
  xor xor_6 (O3, xor_2_out, or_3_out);
  and and_15 (and_15_out, or_4_out, xor_3_out);
  xor xor_7 (O2, xor_3_out, or_4_out);
  and and_16 (and_16_out, Carry_In, xor_4_out);
  xor xor_8 (O1, xor_4_out, Carry_In);
  or or_1 (Overflow, and_13_out, and_9_out);
  or or_2 (or_2_out, and_14_out, and_10_out);
  or or_3 (or_3_out, and_15_out, and_11_out);
  or or_4 (or_4_out, and_16_out, and_12_out);
endmodule

module cpu (
  input  in_1,
  input  in_2,
  input  in_3,
  input  in_4,
  input  in_5,
  input  in_6,
  input  in_7,
  input  in_8,
  input  R_RAM,
  input  W_RAM,
  input  R_RegA,
  input  W_RegA,
  input  R_RegB,
  input  W_RegB,
  input  W_ADD,
  input  W_RegF,
  input  Clock,
  input  R_RegC,
  input  W_RegC,
  input  LDAM,
  input  LDAB,
  input  ADD
);

  wire controlled_buffer_1_out, controlled_buffer_2_out, controlled_buffer_3_out, controlled_buffer_4_out,
       controlled_buffer_5_out, controlled_buffer_6_out, controlled_buffer_7_out, controlled_buffer_8_out,
       controlled_buffer_9_out, controlled_buffer_10_out, controlled_buffer_11_out, controlled_buffer_12_out,
       controlled_buffer_13_out, controlled_buffer_14_out, fourbitadder_1_o1, fourbitadder_1_o2,
       fourbitadder_1_o3, fourbitadder_1_o4, fourbitadder_1_overflow, not_1_out, or_1_out, or_2_out,
       or_3_out, Register_A_stored_1, Register_A_stored_2, Register_A_stored_3, Register_A_stored_4,
       Register_B_stored_1, Register_B_stored_2, Register_B_stored_3, Register_B_stored_4,
       Register_F_stored_1, Register_F_stored_2, Register_Result_stored_1, Register_Result_stored_2,
       Register_Result_stored_3, Register_Result_stored_4, undriven, undriven_2, undriven_3, undriven_4;
  wire [7:0] ram_1_dout;

  assign controlled_buffer_1_out = LDAM ? LDAM : 1'bz;  // Controlled_Buffer controlled_buffer_1
  assign controlled_buffer_2_out = LDAM ? LDAM : 1'bz;  // Controlled_Buffer controlled_buffer_2
  assign controlled_buffer_3_out = LDAB ? LDAB : 1'bz;  // Controlled_Buffer controlled_buffer_3
  assign controlled_buffer_4_out = LDAB ? LDAB : 1'bz;  // Controlled_Buffer controlled_buffer_4
  assign controlled_buffer_5_out = ADD ? ADD : 1'bz;  // Controlled_Buffer controlled_buffer_5
  assign controlled_buffer_6_out = ADD ? ADD : 1'bz;  // Controlled_Buffer controlled_buffer_6
  assign controlled_buffer_7_out = controlled_buffer_3_out ? Register_A_stored_1 : 1'bz;  // Controlled_Buffer controlled_buffer_7
  assign controlled_buffer_8_out = controlled_buffer_3_out ? Register_A_stored_2 : 1'bz;  // Controlled_Buffer controlled_buffer_8
  fourbitreg Register_A (
    .DATA1(controlled_buffer_7_out), .DATA2(controlled_buffer_8_out), .DATA3(controlled_buffer_9_out),
    .DATA4(controlled_buffer_10_out), .S(controlled_buffer_2_out), .C(Clock), .Stored_1(Register_A_stored_1),
    .Stored_2(Register_A_stored_2), .Stored_3(Register_A_stored_3), .Stored_4(Register_A_stored_4));
  assign controlled_buffer_9_out = controlled_buffer_3_out ? Register_A_stored_3 : 1'bz;  // Controlled_Buffer controlled_buffer_9
  assign controlled_buffer_10_out = controlled_buffer_3_out ? Register_A_stored_4 : 1'bz;  // Controlled_Buffer controlled_buffer_10
  assign controlled_buffer_11_out = controlled_buffer_4_out ? controlled_buffer_10_out : 1'bz;  // Controlled_Buffer controlled_buffer_11
  assign controlled_buffer_12_out = controlled_buffer_4_out ? controlled_buffer_9_out : 1'bz;  // Controlled_Buffer controlled_buffer_12
  assign controlled_buffer_13_out = controlled_buffer_4_out ? controlled_buffer_8_out : 1'bz;  // Controlled_Buffer controlled_buffer_13
  assign controlled_buffer_14_out = controlled_buffer_4_out ? controlled_buffer_7_out : 1'bz;  // Controlled_Buffer controlled_buffer_14
  assign controlled_buffer_7_out = undriven_2 ? Register_B_stored_1 : 1'bz;  // Controlled_Buffer controlled_buffer_15
  assign controlled_buffer_8_out = undriven_2 ? Register_B_stored_2 : 1'bz;  // Controlled_Buffer controlled_buffer_16
  assign controlled_buffer_9_out = undriven_2 ? Register_B_stored_3 : 1'bz;  // Controlled_Buffer controlled_buffer_17
  fourbitreg Register_B (
    .DATA1(controlled_buffer_14_out), .DATA2(controlled_buffer_13_out), .DATA3(controlled_buffer_12_out),
    .DATA4(controlled_buffer_11_out), .S(controlled_buffer_4_out), .C(Clock), .Stored_1(Register_B_stored_1),
    .Stored_2(Register_B_stored_2), .Stored_3(Register_B_stored_3), .Stored_4(Register_B_stored_4));
  assign controlled_buffer_10_out = undriven_2 ? Register_B_stored_4 : 1'bz;  // Controlled_Buffer controlled_buffer_18
  fourbitadder fourbitadder_1 (
    .B4(Register_A_stored_4), .B3(Register_A_stored_3), .B2(Register_A_stored_2), .B1(Register_A_stored_1),
    .A4(Register_B_stored_4), .A3(Register_B_stored_3), .A2(Register_B_stored_2), .A1(Register_B_stored_1),
    .Clock(Clock), .Overflow(fourbitadder_1_overflow), .O1(fourbitadder_1_o1), .O2(fourbitadder_1_o2),
    .O3(fourbitadder_1_o3), .O4(fourbitadder_1_o4));  // open: Carry_In
  assign controlled_buffer_7_out = undriven ? Register_Result_stored_1 : 1'bz;  // Controlled_Buffer controlled_buffer_19
  assign controlled_buffer_8_out = undriven ? Register_Result_stored_2 : 1'bz;  // Controlled_Buffer controlled_buffer_20
  fourbitreg Register_Result (
    .DATA1(fourbitadder_1_o1), .DATA2(fourbitadder_1_o2), .DATA3(fourbitadder_1_o3),
    .DATA4(fourbitadder_1_o4), .S(controlled_buffer_6_out), .C(Clock), .Stored_1(Register_Result_stored_1),
    .Stored_2(Register_Result_stored_2), .Stored_3(Register_Result_stored_3),
    .Stored_4(Register_Result_stored_4));
  assign controlled_buffer_9_out = undriven ? Register_Result_stored_3 : 1'bz;  // Controlled_Buffer controlled_buffer_21
  assign controlled_buffer_10_out = undriven ? Register_Result_stored_4 : 1'bz;  // Controlled_Buffer controlled_buffer_22
  or or_1 (or_1_out, Register_Result_stored_1, Register_Result_stored_2);
  or or_2 (or_2_out, Register_Result_stored_3, Register_Result_stored_4);
  or or_3 (or_3_out, or_1_out, or_2_out);
  not not_1 (not_1_out, or_3_out);
  assign controlled_buffer_7_out = undriven_3 ? Register_F_stored_1 : 1'bz;  // Controlled_Buffer controlled_buffer_23
  assign controlled_buffer_8_out = undriven_3 ? Register_F_stored_2 : 1'bz;  // Controlled_Buffer controlled_buffer_24
  fourbitreg Register_F (
    .DATA1(fourbitadder_1_overflow), .DATA2(not_1_out), .S(controlled_buffer_5_out), .C(Clock),
    .Stored_1(Register_F_stored_1), .Stored_2(Register_F_stored_2));  // open: DATA3, DATA4, Stored_3, Stored_4
  RAM ram_1 (
    .addr({in_1, in_2, in_3, in_4, in_5, in_6, in_7, in_8}), .we(undriven_4), .oe(controlled_buffer_1_out),
    .clk(Clock), .dout(ram_1_dout));  // open: din
  assign controlled_buffer_9_out = controlled_buffer_1_out ? ram_1_dout[2] : 1'bz;  // Controlled_Buffer controlled_buffer_25
  assign controlled_buffer_8_out = controlled_buffer_1_out ? ram_1_dout[1] : 1'bz;  // Controlled_Buffer controlled_buffer_26
  assign controlled_buffer_7_out = controlled_buffer_1_out ? ram_1_dout[0] : 1'bz;  // Controlled_Buffer controlled_buffer_27
  assign controlled_buffer_10_out = controlled_buffer_1_out ? ram_1_dout[3] : 1'bz;  // Controlled_Buffer controlled_buffer_28
endmodule

module fourbitreg (
  input  DATA1,
  input  DATA2,
  input  DATA3,
  input  DATA4,
  input  S,
  input  C,
  output Stored_1,
  output Stored_2,
  output Stored_3,
  output Stored_4
);

  wire and_1_out, and_2_out, and_3_out, and_4_out, and_5_out, and_6_out, and_7_out, and_8_out, and_9_out,
       and_10_out, and_11_out, and_12_out, nor_1_out, nor_3_out, nor_5_out, nor_7_out, not_1_out, not_2_out,
       not_3_out, not_4_out;

  and and_1 (and_1_out, S, C);
  and and_2 (and_2_out, S, C);
  and and_3 (and_3_out, S, C);
  not not_1 (not_1_out, DATA4);
  and and_4 (and_4_out, S, C);
  and and_5 (and_5_out, DATA1, and_1_out);
  not not_2 (not_2_out, DATA1);
  and and_6 (and_6_out, not_2_out, and_1_out);
  and and_7 (and_7_out, DATA2, and_2_out);
  not not_3 (not_3_out, DATA2);
  and and_8 (and_8_out, not_3_out, and_2_out);
  and and_9 (and_9_out, DATA3, and_3_out);
  not not_4 (not_4_out, DATA3);
  and and_10 (and_10_out, not_4_out, and_3_out);
  and and_11 (and_11_out, DATA4, and_4_out);
  and and_12 (and_12_out, not_1_out, and_4_out);
  nor nor_1 (nor_1_out, and_5_out, Stored_1);
  nor nor_2 (Stored_1, nor_1_out, and_6_out);
  nor nor_3 (nor_3_out, and_7_out, Stored_2);
  nor nor_4 (Stored_2, nor_3_out, and_8_out);
  nor nor_5 (nor_5_out, and_9_out, Stored_3);
  nor nor_6 (Stored_3, nor_5_out, and_10_out);
  nor nor_7 (nor_7_out, and_11_out, Stored_4);
  nor nor_8 (Stored_4, nor_7_out, and_12_out);
endmodule

module fourbitmux (
  input  A1,
  input  A2,
  input  A3,
  input  A4,
  input  B1,
  input  B2,
  input  B3,
  input  B4,
  input  Switch,
  output O1,
  output O2,
  output O3,
  output O4
);

  wire and_1_out, and_2_out, and_3_out, and_4_out, and_5_out, and_6_out, and_7_out, and_8_out, not_1_out,
       not_2_out, not_3_out, not_4_out, not_5_out;

  not not_1 (not_1_out, Switch);
  not not_2 (not_2_out, not_1_out);
  not not_3 (not_3_out, not_1_out);
  not not_4 (not_4_out, not_1_out);
  not not_5 (not_5_out, not_1_out);
  and and_1 (and_1_out, A1, not_1_out);
  and and_2 (and_2_out, B1, not_2_out);
  and and_3 (and_3_out, A2, not_1_out);
  and and_4 (and_4_out, B2, not_3_out);
  and and_5 (and_5_out, A3, not_1_out);
  and and_6 (and_6_out, B3, not_4_out);
  and and_7 (and_7_out, A4, not_1_out);
  and and_8 (and_8_out, B4, not_5_out);
  or or_1 (O1, and_1_out, and_2_out);
  or or_2 (O2, and_3_out, and_4_out);
  or or_3 (O3, and_5_out, and_6_out);
  or or_4 (O4, and_7_out, and_8_out);
endmodule
